// Logisim project cpuPart1.circ as structural Verilog
module ALU (
  input  [15:0] First_argument,
  input  [15:0] Second_argument,
  input  [3:0] Op_code,
  output [15:0] Output
);

  wire comparator_1_lt, comparator_2_eq, comparator_3_eq, not_1_out;
  wire [3:0] bit_extender_1_out;
  wire [15:0] adder_1_out, AND_0_output, bit_extender_2_out, bit_extender_3_out, bit_extender_4_out,
       bit_extender_5_out, bit_extender_6_out, multiplier_1_out, NOT_3_out, OR_1_output, shifter_1_out,
       shifter_2_out, subtractor_1_out, XOR_2_output;

  Bit_Extender #(.in_width(16), .out_width(4)) bit_extender_1 (.in(Second_argument), .out(bit_extender_1_out));
  assign bit_extender_2_out = {{15{1'b0}}, 1'b1};  // Bit_Extender bit_extender_2
  assign bit_extender_3_out = {{15{1'b0}}, 1'b0};  // Bit_Extender bit_extender_3
  _16_bit_AND AND_0 (.First_argument(First_argument), .Second_argument(Second_argument), .Output(AND_0_output));
  _16_bit_OR OR_1 (.First_argument(First_argument), .Second_argument(Second_argument), .Output(OR_1_output));
  _16_bit_XOR XOR_2 (.First_argument(First_argument), .Second_argument(Second_argument), .Output(XOR_2_output));
  assign NOT_3_out = ~First_argument;  // NOT_Gate NOT_3, 16 bits wide
  Adder #(.width(16)) adder_1 (.a(First_argument), .b(Second_argument), .out(adder_1_out));  // open: cin, cout
  Subtractor #(.width(16)) subtractor_1 (
    .a(First_argument), .b(Second_argument), .out(subtractor_1_out));  // open: bin, bout
  Multiplier #(.width(16)) multiplier_1 (
    .a(First_argument), .b(Second_argument), .out(multiplier_1_out));  // open: cin, cout
  Comparator #(.width(16)) comparator_1 (
    .a(First_argument), .b(Second_argument), .lt(comparator_1_lt));  // open: gt, eq
  assign bit_extender_4_out = {{15{1'b0}}, comparator_1_lt};  // Bit_Extender bit_extender_4
  Shifter #(.width(16)) shifter_1 (.in(First_argument), .\dist (bit_extender_1_out), .out(shifter_1_out));
  Shifter #(.width(16), .shift("ar")) shifter_2 (.in(First_argument), .\dist (bit_extender_1_out), .out(shifter_2_out));
  assign bit_extender_5_out = {{15{1'b0}}, comparator_2_eq};  // Bit_Extender bit_extender_5
  Comparator #(.width(16)) comparator_2 (
    .a(First_argument), .b(bit_extender_3_out), .eq(comparator_2_eq));  // open: gt, lt
  not not_1 (not_1_out, comparator_3_eq);
  Comparator #(.width(16)) comparator_3 (
    .a(First_argument), .b(bit_extender_3_out), .eq(comparator_3_eq));  // open: gt, lt
  assign bit_extender_6_out = {{15{1'b0}}, not_1_out};  // Bit_Extender bit_extender_6
  Multiplexer #(.select(4), .width(16), .enable("false")) multiplexer_1 (
    .in0(AND_0_output), .in1(OR_1_output), .in2(XOR_2_output), .in3(NOT_3_out), .in4(adder_1_out),
    .in5(subtractor_1_out), .in6(multiplier_1_out), .in7(bit_extender_4_out), .in8(shifter_1_out),
    .in9(shifter_2_out), .in10(First_argument), .in11(First_argument), .in12(Second_argument),
    .in13(bit_extender_2_out), .in14(bit_extender_5_out), .in15(bit_extender_6_out), .out(Output),
    .sel(Op_code));
endmodule

module Register_file (
  input  Clock_signal,
  input  Clear_signal,
  input  [15:0] Write_data,
  input  [3:0] Write_address,
  input  Write_enable,
  input  [3:0] Read_address_1,
  input  [3:0] Read_address_2,
  output [15:0] Read_data_1,
  output [15:0] Read_data_2
);

  wire decoder_1_out0, decoder_1_out1, decoder_1_out2, decoder_1_out3, decoder_1_out4, decoder_1_out5,
       decoder_1_out6, decoder_1_out7, decoder_1_out8, decoder_1_out9, decoder_1_out10, decoder_1_out11,
       decoder_1_out12, decoder_1_out13, decoder_1_out14, decoder_1_out15;
  wire [15:0] Register_1_q, Register_2_q, Register_3_q, Register_4_q, Register_5_q, Register_6_q,
       Register_7_q, Register_8_q, Register_9_q, Register_10_q, Register_11_q, Register_12_q, Register_13_q,
       Register_14_q, Register_15_q, Register_16_q;

  Decoder #(.select(4), .disabled(0)) decoder_1 (
    .out0(decoder_1_out0), .out1(decoder_1_out1), .out2(decoder_1_out2), .out3(decoder_1_out3),
    .out4(decoder_1_out4), .out5(decoder_1_out5), .out6(decoder_1_out6), .out7(decoder_1_out7),
    .out8(decoder_1_out8), .out9(decoder_1_out9), .out10(decoder_1_out10), .out11(decoder_1_out11),
    .out12(decoder_1_out12), .out13(decoder_1_out13), .out14(decoder_1_out14), .out15(decoder_1_out15),
    .sel(Write_address), .en(Write_enable));
  Register #(.width(16)) Register_1 (
    .D(Write_data), .en(decoder_1_out0), .Q(Register_1_q), .clk(Clock_signal), .clr(Clear_signal));
  Register #(.width(16)) Register_2 (
    .D(Write_data), .en(decoder_1_out1), .Q(Register_2_q), .clk(Clock_signal), .clr(Clear_signal));
  Register #(.width(16)) Register_3 (
    .D(Write_data), .en(decoder_1_out2), .Q(Register_3_q), .clk(Clock_signal), .clr(Clear_signal));
  Register #(.width(16)) Register_4 (
    .D(Write_data), .en(decoder_1_out3), .Q(Register_4_q), .clk(Clock_signal), .clr(Clear_signal));
  Register #(.width(16)) Register_5 (
    .D(Write_data), .en(decoder_1_out4), .Q(Register_5_q), .clk(Clock_signal), .clr(Clear_signal));
  Register #(.width(16)) Register_6 (
    .D(Write_data), .en(decoder_1_out5), .Q(Register_6_q), .clk(Clock_signal), .clr(Clear_signal));
  Register #(.width(16)) Register_7 (
    .D(Write_data), .en(decoder_1_out6), .Q(Register_7_q), .clk(Clock_signal), .clr(Clear_signal));
  Register #(.width(16)) Register_8 (
    .D(Write_data), .en(decoder_1_out7), .Q(Register_8_q), .clk(Clock_signal), .clr(Clear_signal));
  Register #(.width(16)) Register_9 (
    .D(Write_data), .en(decoder_1_out8), .Q(Register_9_q), .clk(Clock_signal), .clr(Clear_signal));
  Register #(.width(16)) Register_10 (
    .D(Write_data), .en(decoder_1_out9), .Q(Register_10_q), .clk(Clock_signal), .clr(Clear_signal));
  Register #(.width(16)) Register_11 (
    .D(Write_data), .en(decoder_1_out10), .Q(Register_11_q), .clk(Clock_signal), .clr(Clear_signal));
  Register #(.width(16)) Register_12 (
    .D(Write_data), .en(decoder_1_out11), .Q(Register_12_q), .clk(Clock_signal), .clr(Clear_signal));
  Register #(.width(16)) Register_13 (
    .D(Write_data), .en(decoder_1_out12), .Q(Register_13_q), .clk(Clock_signal), .clr(Clear_signal));
  Register #(.width(16)) Register_14 (
    .D(Write_data), .en(decoder_1_out13), .Q(Register_14_q), .clk(Clock_signal), .clr(Clear_signal));
  Register #(.width(16)) Register_15 (
    .D(Write_data), .en(decoder_1_out14), .Q(Register_15_q), .clk(Clock_signal), .clr(Clear_signal));
  Register #(.width(16)) Register_16 (
    .D(Write_data), .en(decoder_1_out15), .Q(Register_16_q), .clk(Clock_signal), .clr(Clear_signal));
  Multiplexer #(.select(4), .width(16), .enable("false")) multiplexer_1 (
    .in0(Register_1_q), .in1(Register_2_q), .in2(Register_3_q), .in3(Register_4_q), .in4(Register_5_q),
    .in5(Register_6_q), .in6(Register_7_q), .in7(Register_8_q), .in8(Register_9_q), .in9(Register_10_q),
    .in10(Register_11_q), .in11(Register_12_q), .in12(Register_13_q), .in13(Register_14_q),
    .in14(Register_15_q), .in15(Register_16_q), .out(Read_data_1), .sel(Read_address_1));
  Multiplexer #(.select(4), .width(16), .enable("false")) multiplexer_2 (
    .in0(Register_1_q), .in1(Register_2_q), .in2(Register_3_q), .in3(Register_4_q), .in4(Register_5_q),
    .in5(Register_6_q), .in6(Register_7_q), .in7(Register_8_q), .in8(Register_9_q), .in9(Register_10_q),
    .in10(Register_11_q), .in11(Register_12_q), .in12(Register_13_q), .in13(Register_14_q),
    .in14(Register_15_q), .in15(Register_16_q), .out(Read_data_2), .sel(Read_address_2));
endmodule

module Screen_memory (
  input  Clock_signal,
  input  Clear_signal,
  input  [15:0] Write_data,
  input  [3:0] Write_address,
  input  Write_enable,
  output [15:0] Output_1,
  output [15:0] Output_2,
  output [15:0] Output_3,
  output [15:0] Output_4,
  output [15:0] Output_5,
  output [15:0] Output_6,
  output [15:0] Output_7,
  output [15:0] Output_8,
  output [15:0] Output_9,
  output [15:0] Output_10,
  output [15:0] Output_11,
  output [15:0] Output_12,
  output [15:0] Output_13,
  output [15:0] Output_14,
  output [15:0] Output_15,
  output [15:0] Output_16
);

  wire decoder_1_out0, decoder_1_out1, decoder_1_out2, decoder_1_out3, decoder_1_out4, decoder_1_out5,
       decoder_1_out6, decoder_1_out7, decoder_1_out8, decoder_1_out9, decoder_1_out10, decoder_1_out11,
       decoder_1_out12, decoder_1_out13, decoder_1_out14, decoder_1_out15;

  Decoder #(.select(4), .disabled(0)) decoder_1 (
    .out0(decoder_1_out0), .out1(decoder_1_out1), .out2(decoder_1_out2), .out3(decoder_1_out3),
    .out4(decoder_1_out4), .out5(decoder_1_out5), .out6(decoder_1_out6), .out7(decoder_1_out7),
    .out8(decoder_1_out8), .out9(decoder_1_out9), .out10(decoder_1_out10), .out11(decoder_1_out11),
    .out12(decoder_1_out12), .out13(decoder_1_out13), .out14(decoder_1_out14), .out15(decoder_1_out15),
    .sel(Write_address), .en(Write_enable));
  Register #(.width(16)) Register_1 (
    .D(Write_data), .en(decoder_1_out0), .Q(Output_1), .clk(Clock_signal), .clr(Clear_signal));
  Register #(.width(16)) Register_2 (
    .D(Write_data), .en(decoder_1_out1), .Q(Output_2), .clk(Clock_signal), .clr(Clear_signal));
  Register #(.width(16)) Register_3 (
    .D(Write_data), .en(decoder_1_out2), .Q(Output_3), .clk(Clock_signal), .clr(Clear_signal));
  Register #(.width(16)) Register_4 (
    .D(Write_data), .en(decoder_1_out3), .Q(Output_4), .clk(Clock_signal), .clr(Clear_signal));
  Register #(.width(16)) Register_5 (
    .D(Write_data), .en(decoder_1_out4), .Q(Output_5), .clk(Clock_signal), .clr(Clear_signal));
  Register #(.width(16)) Register_6 (
    .D(Write_data), .en(decoder_1_out5), .Q(Output_6), .clk(Clock_signal), .clr(Clear_signal));
  Register #(.width(16)) Register_7 (
    .D(Write_data), .en(decoder_1_out6), .Q(Output_7), .clk(Clock_signal), .clr(Clear_signal));
  Register #(.width(16)) Register_8 (
    .D(Write_data), .en(decoder_1_out7), .Q(Output_8), .clk(Clock_signal), .clr(Clear_signal));
  Register #(.width(16)) Register_9 (
    .D(Write_data), .en(decoder_1_out8), .Q(Output_9), .clk(Clock_signal), .clr(Clear_signal));
  Register #(.width(16)) Register_10 (
    .D(Write_data), .en(decoder_1_out9), .Q(Output_10), .clk(Clock_signal), .clr(Clear_signal));
  Register #(.width(16)) Register_11 (
    .D(Write_data), .en(decoder_1_out10), .Q(Output_11), .clk(Clock_signal), .clr(Clear_signal));
  Register #(.width(16)) Register_12 (
    .D(Write_data), .en(decoder_1_out11), .Q(Output_12), .clk(Clock_signal), .clr(Clear_signal));
  Register #(.width(16)) Register_13 (
    .D(Write_data), .en(decoder_1_out12), .Q(Output_13), .clk(Clock_signal), .clr(Clear_signal));
  Register #(.width(16)) Register_14 (
    .D(Write_data), .en(decoder_1_out13), .Q(Output_14), .clk(Clock_signal), .clr(Clear_signal));
  Register #(.width(16)) Register_15 (
    .D(Write_data), .en(decoder_1_out14), .Q(Output_15), .clk(Clock_signal), .clr(Clear_signal));
  Register #(.width(16)) Register_16 (
    .D(Write_data), .en(decoder_1_out15), .Q(Output_16), .clk(Clock_signal), .clr(Clear_signal));
endmodule

module _16_bit_AND (
  input  [15:0] First_argument,
  input  [15:0] Second_argument,
  output [15:0] Output
);

  and bit_1 (Output[0], First_argument[0], Second_argument[0]);
  and bit_2 (Output[1], First_argument[1], Second_argument[1]);
  and bit_3 (Output[2], First_argument[2], Second_argument[2]);
  and bit_4 (Output[3], First_argument[3], Second_argument[3]);
  and bit_5 (Output[4], First_argument[4], Second_argument[4]);
  and bit_6 (Output[5], First_argument[5], Second_argument[5]);
  and bit_7 (Output[6], First_argument[6], Second_argument[6]);
  and bit_8 (Output[7], First_argument[7], Second_argument[7]);
  and bit_9 (Output[8], First_argument[8], Second_argument[8]);
  and bit_10 (Output[9], First_argument[9], Second_argument[9]);
  and bit_11 (Output[10], First_argument[10], Second_argument[10]);
  and bit_12 (Output[11], First_argument[11], Second_argument[11]);
  and bit_13 (Output[12], First_argument[12], Second_argument[12]);
  and bit_14 (Output[13], First_argument[13], Second_argument[13]);
  and bit_15 (Output[14], First_argument[14], Second_argument[14]);
  and bit_16 (Output[15], First_argument[15], Second_argument[15]);
endmodule

module _16_bit_OR (
  input  [15:0] First_argument,
  input  [15:0] Second_argument,
  output [15:0] Output
);

  or bit_1 (Output[0], First_argument[0], Second_argument[0]);
  or bit_2 (Output[1], First_argument[1], Second_argument[1]);
  or bit_3 (Output[2], First_argument[2], Second_argument[2]);
  or bit_4 (Output[3], First_argument[3], Second_argument[3]);
  or bit_5 (Output[4], First_argument[4], Second_argument[4]);
  or bit_6 (Output[5], First_argument[5], Second_argument[5]);
  or bit_7 (Output[6], First_argument[6], Second_argument[6]);
  or bit_8 (Output[7], First_argument[7], Second_argument[7]);
  or bit_9 (Output[8], First_argument[8], Second_argument[8]);
  or bit_10 (Output[9], First_argument[9], Second_argument[9]);
  or bit_11 (Output[10], First_argument[10], Second_argument[10]);
  or bit_12 (Output[11], First_argument[11], Second_argument[11]);
  or bit_13 (Output[12], First_argument[12], Second_argument[12]);
  or bit_14 (Output[13], First_argument[13], Second_argument[13]);
  or bit_15 (Output[14], First_argument[14], Second_argument[14]);
  or bit_16 (Output[15], First_argument[15], Second_argument[15]);
endmodule

module _16_bit_XOR (
  input  [15:0] First_argument,
  input  [15:0] Second_argument,
  output [15:0] Output
);

  xor bit_1 (Output[0], First_argument[0], Second_argument[0]);
  xor bit_2 (Output[1], First_argument[1], Second_argument[1]);
  xor bit_3 (Output[2], First_argument[2], Second_argument[2]);
  xor bit_4 (Output[3], First_argument[3], Second_argument[3]);
  xor bit_5 (Output[4], First_argument[4], Second_argument[4]);
  xor bit_6 (Output[5], First_argument[5], Second_argument[5]);
  xor bit_7 (Output[6], First_argument[6], Second_argument[6]);
  xor bit_8 (Output[7], First_argument[7], Second_argument[7]);
  xor bit_9 (Output[8], First_argument[8], Second_argument[8]);
  xor bit_10 (Output[9], First_argument[9], Second_argument[9]);
  xor bit_11 (Output[10], First_argument[10], Second_argument[10]);
  xor bit_12 (Output[11], First_argument[11], Second_argument[11]);
  xor bit_13 (Output[12], First_argument[12], Second_argument[12]);
  xor bit_14 (Output[13], First_argument[13], Second_argument[13]);
  xor bit_15 (Output[14], First_argument[14], Second_argument[14]);
  xor bit_16 (Output[15], First_argument[15], Second_argument[15]);
endmodule
