// Logisim project flipFlop.circ as structural Verilog: 3 circuits, main circuit main
module main (
  input  [7:0] in_1,
  output [7:0] out_2
);

  wire clock_1_out;
  wire [7:0] adder_1_out;

  Adder adder_1 (.a(out_2), .b(8'h1), .out(adder_1_out));  // open: cin, cout
  Clock clock_1 (.out(clock_1_out));
  register register_1 (.Q(out_2), .Data_bit(adder_1_out), .Clock(clock_1_out));
endmodule

module flipflop (
  input  Data,
  input  Clock,
  output Q,
  output nQ
);

  wire and_1_out, and_2_out, and_3_out, and_4_out, nor_1_out, nor_2_out, not_1_out;

  not not_1 (not_1_out, Clock);
  and and_1 (and_1_out, Data, not_1_out);
  and and_2 (and_2_out, not_1_out, ~Data);  // AND_Gate
  nor nor_1 (nor_1_out, and_1_out, nor_2_out);
  nor nor_2 (nor_2_out, nor_1_out, and_2_out);
  and and_3 (and_3_out, nor_1_out, Clock);
  and and_4 (and_4_out, Clock, nor_2_out);
  nor nor_3 (Q, and_3_out, nQ);
  nor nor_4 (nQ, Q, and_4_out);
endmodule

module register (
  input  [7:0] Data_bit,
  input  Clock,
  output [7:0] Q
);

  wire flipflop_1_nq;

  flipflop flipflop_1 (.Data(Data_bit[0]), .Clock(Clock), .Q(Q[0]), .nQ(flipflop_1_nq));
  flipflop flipflop_2 (.Data(Data_bit[1]), .Clock(Clock), .Q(Q[1]));  // open: nQ
  flipflop flipflop_3 (.Data(Data_bit[2]), .Clock(Clock), .Q(Q[2]));  // open: nQ
  flipflop flipflop_4 (.Data(Data_bit[3]), .Clock(Clock), .Q(Q[3]));  // open: nQ
  flipflop flipflop_5 (.Data(Data_bit[4]), .Clock(Clock), .Q(Q[4]));  // open: nQ
  flipflop flipflop_6 (.Data(Data_bit[5]), .Clock(Clock), .Q(Q[5]));  // open: nQ
  flipflop flipflop_7 (.Data(Data_bit[6]), .Clock(Clock), .Q(Q[6]));  // open: nQ
  flipflop flipflop_8 (.Data(Data_bit[7]), .Clock(Clock), .Q(Q[7]));  // open: nQ
endmodule
