// Logisim project monthAndDay.circ as structural Verilog: 3 circuits, main circuit main
module main (
  input  Leap,
  input  Month,
  input  Month_2,
  input  Month_3,
  input  Month_4,
  input  Day,
  input  Day_2,
  input  Day_3,
  input  Day_4,
  input  Day_5
);

  wire month_to_max_days_1_day0, month_to_max_days_1_day1, or_1_out, two_bit_less_than_or_equal_to_1_output;

  Month_to_Max_Days month_to_max_days_1 (
    .leap(Leap), .month3(Month), .month2(Month_2), .month1(Month_3), .month0(Month_4),
    .day1(month_to_max_days_1_day1), .day0(month_to_max_days_1_day0));
  Two_Bit_Less_Than_or_Equal_To two_bit_less_than_or_equal_to_1 (
    .group21(month_to_max_days_1_day1), .group20(month_to_max_days_1_day0), .group11(Day_4), .group10(Day_5),
    .\output (two_bit_less_than_or_equal_to_1_output));
  LED led_1 (.in(or_1_out));
  or or_1 (or_1_out, ~Day, ~Day_2, ~Day_3, two_bit_less_than_or_equal_to_1_output);  // OR_Gate
endmodule

module Month_to_Max_Days (
  input  leap,
  input  month3,
  input  month2,
  input  month1,
  input  month0,
  output day1,
  output day0
);

  wire and_1_out, and_2_out, and_3_out, and_4_out, not_1_out, not_2_out, not_3_out, not_4_out, not_5_out,
       not_6_out;

  not not_1 (not_1_out, month0);
  not not_2 (not_2_out, month3);
  not not_3 (not_3_out, month0);
  not not_4 (not_4_out, month3);
  not not_5 (not_5_out, month2);
  not not_6 (not_6_out, month1);
  or or_1 (day1, not_1_out, month1, month2, month3);
  and and_1 (and_1_out, not_2_out, not_3_out);
  and and_2 (and_2_out, month2, month1);
  and and_3 (and_3_out, month3, month0);
  and and_4 (and_4_out, leap, not_4_out, not_5_out, not_6_out);
  or or_2 (day0, and_1_out, and_2_out, and_3_out, and_4_out);
endmodule

module Two_Bit_Less_Than_or_Equal_To (
  input  group21,
  input  group20,
  input  group11,
  input  group10,
  output \output 
);

  wire and_1_out, and_2_out, and_3_out, and_4_out, and_5_out, not_1_out, not_2_out, not_3_out, not_4_out,
       not_5_out;

  not not_1 (not_1_out, group11);
  and and_1 (and_1_out, not_1_out, not_2_out);
  not not_2 (not_2_out, group10);
  and and_2 (and_2_out, group20, not_3_out);
  not not_3 (not_3_out, group11);
  and and_3 (and_3_out, group21, not_4_out);
  not not_4 (not_4_out, group11);
  and and_4 (and_4_out, group21, not_5_out);
  not not_5 (not_5_out, group10);
  and and_5 (and_5_out, group21, group20);
  or or_1 (\output , and_1_out, and_2_out, and_3_out, and_4_out, and_5_out);
endmodule
