// Logisim project switch.circ as structural Verilog: 1 circuit, main circuit main
module main (
  input  Rock,
  input  Paper,
  input  Scissor,
  input  Rock_2,
  input  Paper_2,
  input  Scissor_2
);

  wire transistor_1_out, transistor_2_out, transistor_3_out, transistor_4_out, transistor_5_out,
       transistor_6_out, transistor_9_out, transistor_12_out;

  LED led_1 (.in(transistor_1_out));
  Transistor #(.\type ("n")) transistor_1 (.in(transistor_3_out), .out(transistor_1_out), .gate(Rock_2));
  Transistor #(.\type ("n")) transistor_2 (.in(1'b1), .out(transistor_2_out), .gate(Rock));
  Transistor #(.\type ("n")) transistor_3 (.in(1'b1), .out(transistor_3_out), .gate(Paper));
  Transistor #(.\type ("n")) transistor_4 (.in(1'b1), .out(transistor_4_out), .gate(Scissor));
  Transistor #(.gate("br")) transistor_5 (.in(transistor_2_out), .out(transistor_5_out), .gate(Rock_2));
  Transistor #(.gate("br")) transistor_6 (.in(transistor_3_out), .out(transistor_6_out), .gate(Rock_2));
  Transistor #(.\type ("n")) transistor_7 (.in(transistor_4_out), .out(transistor_1_out), .gate(Paper_2));
  Transistor #(.\type ("n")) transistor_8 (.in(transistor_5_out), .out(transistor_1_out), .gate(Scissor_2));
  Transistor #(.\type ("n"), .gate("br")) transistor_9 (.in(transistor_2_out), .out(transistor_9_out), .gate(Paper_2));
  Transistor #(.gate("br")) transistor_10 (.in(transistor_5_out), .out(transistor_9_out), .gate(Scissor_2));
  Transistor #(.\type ("n"), .gate("br")) transistor_11 (
    .in(transistor_3_out), .out(transistor_9_out), .gate(Scissor_2));
  Transistor #(.gate("br")) transistor_12 (.in(transistor_4_out), .out(transistor_12_out), .gate(Paper_2));
  LED led_2 (.in(transistor_9_out));
  Transistor #(.gate("br")) transistor_13 (.in(transistor_6_out), .out(transistor_9_out), .gate(Paper_2));
  Transistor #(.\type ("n"), .gate("br")) transistor_14 (.in(transistor_4_out), .out(transistor_9_out), .gate(Rock_2));
  Transistor #(.gate("br")) transistor_15 (.in(transistor_12_out), .out(transistor_9_out), .gate(Scissor_2));

  // Notes on the sheet:
  //   Player 1 Wins!
  //   Player 1
  //   Player 2 Wins!
  //   Player 2
endmodule
