// Logisim project tictactoe.circ as structural Verilog: 1 circuit, main circuit main
module main (
  input  in_1,
  input  in_2,
  input  in_3,
  input  in_4,
  input  in_5,
  input  in_6,
  input  in_7,
  input  in_8,
  input  in_9
);

  wire and_1_out, and_2_out, and_3_out, and_4_out, and_5_out, and_6_out, and_7_out, and_8_out, and_9_out,
       and_10_out, and_11_out, and_12_out, and_13_out, and_14_out, and_15_out, and_16_out, and_17_out,
       and_18_out, and_19_out, and_20_out, and_21_out, and_22_out, and_23_out, and_24_out, and_25_out,
       and_26_out, and_27_out, and_28_out, nand_1_out, not_1_out, or_1_out, or_2_out;

  and and_1 (and_1_out, in_1, in_2, in_3);
  and and_2 (and_2_out, ~in_1, ~in_2, ~in_3);  // AND_Gate
  and and_3 (and_3_out, in_1, in_2, in_3);
  and and_4 (and_4_out, ~in_1, ~in_2, ~in_3);  // AND_Gate
  and and_5 (and_5_out, in_1, in_2, in_3);
  and and_6 (and_6_out, ~in_1, ~in_2, ~in_3);  // AND_Gate
  and and_7 (and_7_out, in_1, in_5, in_9);
  and and_8 (and_8_out, ~in_1, ~in_5, ~in_9);  // AND_Gate
  LED Player_0 (.in(not_1_out));
  and and_9 (and_9_out, in_4, in_7, in_1);
  and and_10 (and_10_out, ~in_4, ~in_7, ~in_1);  // AND_Gate
  or or_1 (or_1_out, and_2_out, and_4_out, and_6_out, and_8_out, and_10_out, and_12_out, and_14_out, and_16_out, and_20_out, and_24_out, and_28_out, and_19_out, and_23_out, and_27_out);
  not not_1 (not_1_out, nand_1_out);
  and and_11 (and_11_out, in_5, in_8, in_2);
  and and_12 (and_12_out, ~in_5, ~in_8, ~in_2);  // AND_Gate
  nand nand_1 (nand_1_out, or_1_out, ~or_2_out);  // NAND_Gate
  LED Player_1 (.in(nand_1_out));
  or or_2 (or_2_out, and_1_out, and_3_out, and_5_out, and_7_out, and_9_out, and_13_out, and_15_out, and_11_out, and_17_out, and_21_out, and_25_out, and_18_out, and_22_out, and_26_out);
  and and_13 (and_13_out, in_6, in_9, in_3);
  and and_14 (and_14_out, ~in_6, ~in_9, ~in_3);  // AND_Gate
  and and_15 (and_15_out, in_7, in_5, in_3);
  and and_16 (and_16_out, ~in_7, ~in_5, ~in_3);  // AND_Gate
  and and_17 (and_17_out, in_4, in_5, in_6);
  and and_18 (and_18_out, in_9, in_8, in_9);
  and and_19 (and_19_out, ~in_5, ~in_4, ~in_4);  // AND_Gate
  and and_20 (and_20_out, ~in_8, ~in_7, ~in_9);  // AND_Gate
  and and_21 (and_21_out, in_4, in_5, in_6);
  and and_22 (and_22_out, in_7, in_8, in_9);
  and and_23 (and_23_out, ~in_5, ~in_4, ~in_4);  // AND_Gate
  and and_24 (and_24_out, ~in_8, ~in_7, ~in_9);  // AND_Gate
  and and_25 (and_25_out, in_4, in_5, in_6);
  and and_26 (and_26_out, in_7, in_8, in_9);
  and and_27 (and_27_out, ~in_5, ~in_4, ~in_4);  // AND_Gate
  and and_28 (and_28_out, ~in_8, ~in_7, ~in_9);  // AND_Gate
endmodule
