// Logisim project gate.circ as structural Verilog: 1 circuit, main circuit main
module main (
  input  in_1,
  input  in_2
);

  wire _0_out, _1_out, _2_out, _3_out, or_1_out, or_2_out, or_3_out, or_4_out, or_5_out, or_6_out;

  and _0 (_0_out, ~in_1, ~in_2);  // AND_Gate
  and _1 (_1_out, ~in_1, in_2);  // AND_Gate
  and _2 (_2_out, in_1, ~in_2);  // AND_Gate
  and _3 (_3_out, in_1, in_2);
  or or_1 (or_1_out, _0_out, in_2);
  or or_2 (or_2_out, _2_out, _3_out);
  or or_3 (or_3_out, or_1_out, _2_out, _1_out);
  or or_4 (or_4_out, _2_out, _3_out, _0_out);
  or or_5 (or_5_out, _2_out, _3_out, _0_out);
  or or_6 (or_6_out, _0_out, _2_out);
  _7_Segment_Display u_7_segment_display_1 (.f(1'b1), .a(1'b1), .b(1'b1), .e(1'b1), .d(1'b1), .c(1'b1));  // open: g, dp
  _7_Segment_Display u_7_segment_display_2 (
    .g(or_2_out), .f(_0_out), .a(or_5_out), .b(or_3_out), .e(or_6_out), .d(or_4_out), .c(or_1_out));  // open: dp
endmodule
