// Logisim project transistor.circ as structural Verilog: 1 circuit, main circuit main
module main (
);

  wire button_1_out, transistor_1_out;

  Button button_1 (.out(button_1_out));
  Transistor #(.\type ("n")) transistor_1 (.in(1'b1), .out(transistor_1_out), .gate(button_1_out));
  LED led_1 (.in(transistor_1_out));
endmodule
